# Fritzing sketch stepperResonance (saved by Fritzing 0.9.1b)
breadboards: 1

parts:
  Parte1 = Arduino Uno (Rev3)
  R1 = Resistor [tolerance=±5% resistance=220 package=THT]
  R2 = Resistor [tolerance=±5% resistance=220 package=THT]
  S1 = Pushbutton [package="[THT]"]
  S2 = Pushbutton [package="[THT]"]
  MOTOR1 = 28BYJ-48 Stepper Motor
  X1 = X113647 Stepper Driver Board [package=board]

nets:
  N1: Parte1.D8, X1.IN1
  N2: Parte1.D9_PWM, X1.IN2
  N3: Parte1.D10_PWM/SS, X1.IN3
  N4: Parte1.D11_PWM/MOSI, X1.IN4
  N5: Parte1.D2, R1.Pin_1, S2.Pin_3, S2.Pin_4
  N6: Parte1.D3_PWM, R2.Pin_1, S1.Pin_3, S1.Pin_4
  N7: Parte1.5V, S1.Pin_1, S1.Pin_2, S2.Pin_1, S2.Pin_2, X1.+V
  GND: Parte1.GND, R1.Pin_0, R2.Pin_0, X1.GND
  N8: MOTOR1.BLUE, X1.BLUE
  N9: MOTOR1.PINK, X1.PINK
  N10: MOTOR1.RED, X1.RED
  N11: MOTOR1.ORANGE, X1.ORANGE
  N12: MOTOR1.YELLOW, X1.YELLOW

custom parts:
  28BYJ-48 Stepper Motor: 28BYJ-48 gear-reduction stepper motor (small)
  X113647 Stepper Driver Board: A common stepper motor driver board based on ULN2003APG darlington array
